// Logisim project jrmips-dmd113.circ as structural Verilog: 9 circuits, main circuit main
module main (
);

  wire alu_1_brancheqzero, alu_1_branchgreater, alu_1_branchless, BN_out, BP_out, branchcontrol_1_bn,
       branchcontrol_1_bp, branchcontrol_1_bx, branchcontrol_1_bz, BX_out, BZ_out, Clock_out, Control_addi,
       Control_alusrc, Control_branch, Control_halt, Control_memread, Control_memtoreg, Control_memwrite,
       Control_put, Control_regwrite, Control_shift, controlled_buffer_1_out, not_1_out, not_2_out,
       not_3_out, or_1_out, or_2_out, or_3_out, shiftcontrol_1_leftorright, shiftcontrol_1_shamtorreg;
  wire [1:0] aluctrl_1_aluop;
  wire [2:0] jumpcontrol_1_output;
  wire [3:0] multiplexer_4_out, register_1_q_2;
  wire [7:0] adder_1_out, multiplexer_2_out, multiplexer_3_out, multiplexer_7_out, multiplexer_8_out, PC_q;
  wire [11:0] register_1_q;
  wire [15:0] alu_1_result, bit_extender_1_out, bit_extender_2_out, bit_extender_3_out, multiplexer_1_out,
       multiplexer_5_out, multiplexer_6_out, multiplexer_9_out, multiplexer_10_out, multiplexer_11_out,
       ram_1_data, registers_1_readdata1, registers_1_readdata2, rom_1_data, shifter_1_out, shifter_2_out;
  wire [15:8] multiplexer_8_out_2;

  Clock Clock (.out(Clock_out));
  LED Halt (.in(Control_halt));
  not not_1 (not_1_out, Control_halt);
  assign controlled_buffer_1_out = Control_halt ? not_1_out : 1'bz;  // Controlled_Buffer controlled_buffer_1
  Register PC (.D(multiplexer_2_out), .en(controlled_buffer_1_out), .Q(PC_q), .clk(Clock_out));  // open: clr
  Adder adder_1 (.a(8'h1), .b(PC_q), .out(adder_1_out));  // open: cin, cout
  assign bit_extender_1_out = {{8{1'b0}}, adder_1_out};  // Bit_Extender bit_extender_1
  Multiplexer #(.width(16), .enable("false")) multiplexer_1 (
    .in0(multiplexer_11_out), .in1(bit_extender_1_out), .out(multiplexer_1_out), .sel(jumpcontrol_1_output[1]));
  ROM #(.dataWidth(16)) rom_1 (.addr(PC_q), .data(rom_1_data), .sel(1'b1));
  Hex_Digit_Display hex_digit_display_1 (.value(register_1_q_2));  // open: dp
  Hex_Digit_Display hex_digit_display_2 (.value(register_1_q[11:8]));  // open: dp
  Register #(.width(16)) register_1 (
    .D(registers_1_readdata1), .en(Control_put), .Q({register_1_q_2, register_1_q}), .clk(Clock_out));  // open: clr
  Hex_Digit_Display hex_digit_display_3 (.value(register_1_q[3:0]));  // open: dp
  Hex_Digit_Display hex_digit_display_4 (.value(register_1_q[7:4]));  // open: dp
  Multiplexer #(.width(8), .enable("false")) multiplexer_2 (
    .in0(multiplexer_7_out), .in1(multiplexer_3_out), .out(multiplexer_2_out), .sel(or_1_out));
  Multiplexer #(.width(8), .enable("false")) multiplexer_3 (
    .in0(rom_1_data[8:1]), .in1(registers_1_readdata1[7:0]), .out(multiplexer_3_out),
    .sel(jumpcontrol_1_output[2]));
  JumpControl jumpcontrol_1 (.Opcode(rom_1_data[15:12]), .Output(jumpcontrol_1_output));
  BranchControl branchcontrol_1 (
    .Opcode(rom_1_data[15:12]), .bp(branchcontrol_1_bp), .bn(branchcontrol_1_bn), .bx(branchcontrol_1_bx),
    .bz(branchcontrol_1_bz));
  ShiftControl shiftcontrol_1 (
    .Opcode(rom_1_data[15:12]), .Subop(rom_1_data[0]), .LeftOrRight(shiftcontrol_1_leftorright),
    .ShamtOrReg(shiftcontrol_1_shamtorreg));
  Control Control (
    .Opcode(rom_1_data[15:12]), .Subop(rom_1_data[0]), .ALUSrc(Control_alusrc), .MemToReg(Control_memtoreg),
    .RegWrite(Control_regwrite), .MemRead(Control_memread), .MemWrite(Control_memwrite),
    .Branch(Control_branch), .Halt(Control_halt), .Put(Control_put), .Addi(Control_addi),
    .Shift(Control_shift));
  Registers registers_1 (
    .ReadRegister1(rom_1_data[11:9]), .ReadRegister2(rom_1_data[8:6]), .WriteRegister(rom_1_data[11:9]),
    .WriteData(multiplexer_1_out), .Clock(Clock_out), .writeEnable(Control_regwrite),
    .ReadData1(registers_1_readdata1), .ReadData2(registers_1_readdata2));  // open: Reset
  Multiplexer #(.width(4), .enable("false")) multiplexer_4 (
    .in0(rom_1_data[4:1]), .in1(registers_1_readdata2[3:0]), .out(multiplexer_4_out),
    .sel(shiftcontrol_1_shamtorreg));
  or or_1 (or_1_out, jumpcontrol_1_output[0], jumpcontrol_1_output[1], jumpcontrol_1_output[2]);
  ALUCtrl aluctrl_1 (.Opcode(rom_1_data[15:12]), .Subop(rom_1_data[0]), .ALUOp(aluctrl_1_aluop));
  Multiplexer #(.width(16), .enable("false")) multiplexer_5 (
    .in0(registers_1_readdata2), .in1(multiplexer_6_out), .out(multiplexer_5_out), .sel(Control_alusrc));
  assign bit_extender_2_out = {{8{1'b0}}, rom_1_data[8:1]};  // Bit_Extender bit_extender_2
  Multiplexer #(.width(16), .enable("false")) multiplexer_6 (
    .in0(bit_extender_2_out), .in1(bit_extender_3_out), .out(multiplexer_6_out), .sel(Control_addi));
  assign bit_extender_3_out = {{8{rom_1_data[8]}}, rom_1_data[8:1]};  // Bit_Extender bit_extender_3
  Shifter #(.width(16)) shifter_1 (.in(registers_1_readdata1), .\dist (multiplexer_4_out), .out(shifter_1_out));
  Shifter #(.width(16), .shift("lr")) shifter_2 (
    .in(registers_1_readdata1), .\dist (multiplexer_4_out), .out(shifter_2_out));
  Multiplexer #(.width(8), .enable("false")) multiplexer_7 (
    .in0(adder_1_out), .in1(rom_1_data[8:1]), .out(multiplexer_7_out), .sel(or_3_out));
  not not_2 (not_2_out, alu_1_brancheqzero);
  or or_2 (or_2_out, Control_memwrite, Control_memread);
  ALU alu_1 (
    .A(registers_1_readdata1), .B(multiplexer_5_out), .Operation(aluctrl_1_aluop),
    .BranchEqZero(alu_1_brancheqzero), .BranchGreater(alu_1_branchgreater), .BranchLess(alu_1_branchless),
    .Result(alu_1_result));
  not not_3 (not_3_out, or_2_out);
  Multiplexer #(.width(16), .enable("false")) multiplexer_8 (
    .in0(registers_1_readdata2), .in1(alu_1_result), .out({multiplexer_8_out_2, multiplexer_8_out}),
    .sel(not_3_out));
  Multiplexer #(.width(16), .enable("false")) multiplexer_9 (
    .in0(shifter_1_out), .in1(shifter_2_out), .out(multiplexer_9_out), .sel(shiftcontrol_1_leftorright));
  and BP (BP_out, Control_branch, alu_1_branchgreater, branchcontrol_1_bp);
  and BN (BN_out, Control_branch, alu_1_branchless, branchcontrol_1_bn);
  and BX (BX_out, not_2_out, Control_branch, branchcontrol_1_bx);
  and BZ (BZ_out, alu_1_brancheqzero, Control_branch, branchcontrol_1_bz);
  or or_3 (or_3_out, BP_out, BN_out, BX_out, BZ_out);
  RAM #(.dataWidth(16), .bus("separate")) ram_1 (
    .addr(multiplexer_8_out), .din(registers_1_readdata1), .data(ram_1_data), .str(Control_memwrite),
    .sel(1'b1), .clk(Clock_out), .ld(Control_memread));  // open: clr
  Multiplexer #(.width(16), .enable("false")) multiplexer_10 (
    .in0({multiplexer_8_out_2, multiplexer_8_out}), .in1(ram_1_data), .out(multiplexer_10_out),
    .sel(Control_memtoreg));
  Multiplexer #(.width(16), .enable("false")) multiplexer_11 (
    .in0(multiplexer_10_out), .in1(multiplexer_9_out), .out(multiplexer_11_out), .sel(Control_shift));

  // Notes on the sheet:
  //   Property of:
  //   Devansh Desai
  //   University of Pittsburgh
  //   CS 0447
  //   04/17/15
  //   Property of:
  //   Devansh Desai
  //   University of Pittsburgh
  //   CS 0447
  //   04/17/15
  //   CS 0447
  //   04/17/15
  //   PC Incrementer
  //   Put Register
  //   Property of:
  //   Devansh Desai
  //   University of Pittsburgh
  //   INSTRUCTIONS
  //   LED Display
  //   Jump Check
  //   Shift Control
  //   Jump Control
  //   Branch Control
  //   Registers
  //   ALU Control
  //   PCSrc
  //   ALU
  //   Shifters
  //   Branch Check
  //   RAM
  //   Property of:
  //   Devansh Desai
  //   University of Pittsburgh
  //   CS 0447
  //   04/17/15
  //   Property of:
  //   Devansh Desai
  //   University of Pittsburgh
  //   CS 0447
  //   04/17/15
endmodule

module Registers (
  input  writeEnable,
  input  [2:0] ReadRegister1,
  input  [2:0] ReadRegister2,
  input  [2:0] WriteRegister,
  input  [15:0] WriteData,
  input  Clock,
  input  Reset,
  output [15:0] ReadData1,
  output [15:0] ReadData2
);

  wire demultiplexer_1_out0, demultiplexer_1_out1, demultiplexer_1_out2, demultiplexer_1_out3,
       demultiplexer_1_out4, demultiplexer_1_out5, demultiplexer_1_out6, demultiplexer_1_out7;
  wire [15:0] register_1_q, register_2_q, register_3_q, register_4_q, register_5_q, register_6_q,
       register_7_q, register_8_q;

  Demultiplexer #(.select(3), .enable("false")) demultiplexer_1 (
    .out0(demultiplexer_1_out0), .out1(demultiplexer_1_out1), .out2(demultiplexer_1_out2),
    .out3(demultiplexer_1_out3), .out4(demultiplexer_1_out4), .out5(demultiplexer_1_out5),
    .out6(demultiplexer_1_out6), .out7(demultiplexer_1_out7), .in(writeEnable), .sel(WriteRegister));
  Register #(.width(16)) register_1 (
    .D(WriteData), .en(demultiplexer_1_out0), .Q(register_1_q), .clk(Clock), .clr(Reset));
  Register #(.width(16)) register_2 (
    .D(WriteData), .en(demultiplexer_1_out1), .Q(register_2_q), .clk(Clock), .clr(Reset));
  Register #(.width(16)) register_3 (
    .D(WriteData), .en(demultiplexer_1_out2), .Q(register_3_q), .clk(Clock), .clr(Reset));
  Register #(.width(16)) register_4 (
    .D(WriteData), .en(demultiplexer_1_out3), .Q(register_4_q), .clk(Clock), .clr(Reset));
  Register #(.width(16)) register_5 (
    .D(WriteData), .en(demultiplexer_1_out4), .Q(register_5_q), .clk(Clock), .clr(Reset));
  Register #(.width(16)) register_6 (
    .D(WriteData), .en(demultiplexer_1_out5), .Q(register_6_q), .clk(Clock), .clr(Reset));
  Register #(.width(16)) register_7 (
    .D(WriteData), .en(demultiplexer_1_out6), .Q(register_7_q), .clk(Clock), .clr(Reset));
  Register #(.width(16)) register_8 (
    .D(WriteData), .en(demultiplexer_1_out7), .Q(register_8_q), .clk(Clock), .clr(Reset));
  Multiplexer #(.select(3), .width(16), .enable("false")) multiplexer_1 (
    .in0(register_1_q), .in1(register_2_q), .in2(register_3_q), .in3(register_4_q), .in4(register_5_q),
    .in5(register_6_q), .in6(register_7_q), .in7(register_8_q), .out(ReadData1), .sel(ReadRegister1));
  Multiplexer #(.select(3), .width(16), .enable("false")) multiplexer_2 (
    .in0(register_1_q), .in1(register_2_q), .in2(register_3_q), .in3(register_4_q), .in4(register_5_q),
    .in5(register_6_q), .in6(register_7_q), .in7(register_8_q), .out(ReadData2), .sel(ReadRegister2));

  // Notes on the sheet:
  //   Property of:
  //   Devansh Desai
  //   University of Pittsburgh
  //   CS 0447
  //   04/17/15
  //   Property of:
  //   Devansh Desai
  //   University of Pittsburgh
  //   CS 0447
  //   04/17/15
endmodule

module ALU (
  input  [15:0] A,
  input  [15:0] B,
  input  [1:0] Operation,
  output [15:0] Result,
  output BranchEqZero,
  output BranchGreater,
  output BranchLess
);

  wire [15:0] adder_1_out, AND_out, NOR_out, subtractor_1_out;

  assign AND_out = A & B;  // AND_Gate AND, 16 bits wide
  Subtractor #(.width(16)) subtractor_1 (.a(A), .b(B), .out(subtractor_1_out), .bin(1'b0));  // open: bout
  Comparator #(.width(16)) comparator_1 (.a(A), .b({16{1'b0}}), .eq(BranchEqZero));  // open: gt, lt
  Comparator #(.width(16)) comparator_2 (.a(A), .b({16{1'b0}}), .gt(BranchGreater));  // open: eq, lt
  Comparator #(.width(16)) comparator_3 (.a(A), .b({16{1'b0}}), .lt(BranchLess));  // open: gt, eq
  assign NOR_out = ~(A | B);  // NOR_Gate NOR, 16 bits wide
  Adder #(.width(16)) adder_1 (.a(A), .b(B), .out(adder_1_out), .cin(1'b0));  // open: cout
  Multiplexer #(.select(2), .width(16), .enable("false")) multiplexer_1 (
    .in0(AND_out), .in1(NOR_out), .in2(adder_1_out), .in3(subtractor_1_out), .out(Result), .sel(Operation));

  // Notes on the sheet:
  //   Property of:
  //   Devansh Desai
  //   University of Pittsburgh
  //   CS 0447
  //   04/17/15
  //   00 - AND
  //   01 - NOR
  //   10 - ADD
  //   11 - SUB
endmodule

module Control (
  input  [3:0] Opcode,
  input  Subop,
  output ALUSrc,
  output MemToReg,
  output RegWrite,
  output MemRead,
  output MemWrite,
  output Branch,
  output Halt,
  output Put,
  output Addi,
  output Shift
);

  wire and_1_out, and_2_out, and_4_out, and_5_out, and_6_out, and_7_out, and_14_out, and_15_out, not_1_out,
       not_2_out, not_3_out, not_4_out, not_5_out, not_6_out, not_7_out, not_8_out, not_9_out, not_10_out,
       not_11_out, not_12_out, not_13_out, not_14_out, not_15_out, not_16_out, not_17_out, not_18_out,
       not_19_out, not_20_out, not_21_out, not_22_out, not_23_out, not_24_out, not_25_out, not_26_out,
       not_27_out, not_28_out, not_29_out, not_30_out, not_31_out, not_32_out, not_33_out, not_34_out;

  not not_1 (not_1_out, Opcode[3]);
  not not_2 (not_2_out, Opcode[2]);
  not not_3 (not_3_out, Opcode[0]);
  not not_4 (not_4_out, Opcode[3]);
  not not_5 (not_5_out, Opcode[3]);
  not not_6 (not_6_out, Opcode[1]);
  not not_7 (not_7_out, Subop);
  not not_8 (not_8_out, Opcode[1]);
  not not_9 (not_9_out, Opcode[3]);
  not not_10 (not_10_out, Opcode[1]);
  not not_11 (not_11_out, Subop);
  not not_12 (not_12_out, Opcode[3]);
  not not_13 (not_13_out, Opcode[1]);
  not not_14 (not_14_out, Opcode[2]);
  not not_15 (not_15_out, Opcode[3]);
  not not_16 (not_16_out, Opcode[0]);
  not not_17 (not_17_out, Opcode[3]);
  not not_18 (not_18_out, Opcode[3]);
  not not_19 (not_19_out, Opcode[2]);
  not not_20 (not_20_out, Opcode[0]);
  not not_21 (not_21_out, Subop);
  not not_22 (not_22_out, Opcode[3]);
  not not_23 (not_23_out, Opcode[2]);
  not not_24 (not_24_out, Opcode[3]);
  not not_25 (not_25_out, Opcode[1]);
  not not_26 (not_26_out, Opcode[0]);
  and and_1 (and_1_out, not_1_out, not_2_out, Opcode[1], not_3_out);
  and and_2 (and_2_out, not_4_out, Opcode[2], Opcode[1], Opcode[0]);
  and and_3 (MemToReg, not_5_out, Opcode[2], not_6_out, Opcode[0], not_7_out);
  not not_27 (not_27_out, Opcode[3]);
  and and_4 (and_4_out, not_27_out, not_28_out);
  not not_28 (not_28_out, Opcode[2]);
  not not_29 (not_29_out, Opcode[3]);
  and and_5 (and_5_out, not_29_out, not_30_out, not_31_out);
  not not_30 (not_30_out, Opcode[1]);
  not not_31 (not_31_out, Opcode[0]);
  not not_32 (not_32_out, Opcode[3]);
  and and_6 (and_6_out, not_32_out, not_33_out, not_34_out);
  not not_33 (not_33_out, Opcode[1]);
  not not_34 (not_34_out, Subop);
  and and_7 (and_7_out, Opcode[3], Opcode[2], not_8_out, Opcode[0]);
  and and_8 (MemRead, not_9_out, Opcode[2], not_10_out, Opcode[0], not_11_out);
  and and_9 (MemWrite, not_12_out, Opcode[2], not_13_out, Opcode[0], Subop);
  and and_10 (Branch, Opcode[3], not_14_out);
  and and_11 (Halt, not_15_out, Opcode[2], Opcode[1], not_16_out);
  and and_12 (Put, not_17_out, Opcode[2], Opcode[1], Opcode[0]);
  and and_13 (Addi, not_18_out, not_19_out, Opcode[1], not_20_out, not_21_out);
  and and_14 (and_14_out, not_22_out, not_23_out, Opcode[1], Opcode[0]);
  and and_15 (and_15_out, not_24_out, Opcode[2], not_25_out, not_26_out);
  or or_1 (ALUSrc, and_1_out, and_2_out);
  or or_2 (RegWrite, and_4_out, and_5_out, and_6_out, and_7_out);
  or or_3 (Shift, and_14_out, and_15_out);

  // Notes on the sheet:
  //   Property of:
  //   Devansh Desai
  //   University of Pittsburgh
  //   CS 0447
  //   04/17/15
endmodule

module BranchControl (
  input  [3:0] Opcode,
  output bp,
  output bn,
  output bx,
  output bz
);

  wire not_1_out, not_2_out, not_3_out, not_4_out, not_5_out, not_6_out, not_7_out, not_8_out;

  not not_1 (not_1_out, Opcode[2]);
  not not_2 (not_2_out, Opcode[1]);
  not not_3 (not_3_out, Opcode[0]);
  not not_4 (not_4_out, Opcode[2]);
  not not_5 (not_5_out, Opcode[1]);
  not not_6 (not_6_out, Opcode[2]);
  not not_7 (not_7_out, Opcode[0]);
  not not_8 (not_8_out, Opcode[2]);
  and and_1 (bp, Opcode[3], not_1_out, not_2_out, not_3_out);
  and and_2 (bn, Opcode[3], not_4_out, not_5_out, Opcode[0]);
  and and_3 (bx, Opcode[3], not_6_out, Opcode[1], not_7_out);
  and and_4 (bz, Opcode[3], not_8_out, Opcode[1], Opcode[0]);

  // Notes on the sheet:
  //   Property of:
  //   Devansh Desai
  //   University of Pittsburgh
  //   CS 0447
  //   04/17/15
endmodule

module JumpControl (
  input  [3:0] Opcode,
  output [2:0] Output
);

  wire not_1_out, not_2_out, not_3_out, not_4_out;

  not not_1 (not_1_out, Opcode[1]);
  not not_2 (not_2_out, Opcode[0]);
  not not_3 (not_3_out, Opcode[1]);
  not not_4 (not_4_out, Opcode[0]);
  and and_1 (Output[2], Opcode[3], Opcode[2], not_1_out, not_2_out);
  and and_2 (Output[1], Opcode[3], Opcode[2], not_3_out, Opcode[0]);
  and and_3 (Output[0], Opcode[3], Opcode[2], Opcode[1], not_4_out);
endmodule

module ALUCtrl (
  input  [3:0] Opcode,
  input  Subop,
  output [1:0] ALUOp
);

  wire not_1_out, not_2_out, not_3_out;

  not not_1 (not_1_out, Opcode[3]);
  not not_2 (not_2_out, Opcode[2]);
  not not_3 (not_3_out, Opcode[1]);
  or or_1 (ALUOp[1], Opcode[0], Opcode[1], Opcode[2], Opcode[3]);
  and and_1 (ALUOp[0], not_1_out, not_2_out, not_3_out, Subop);

  // Notes on the sheet:
  //   Property of:
  //   Devansh Desai
  //   University of Pittsburgh
  //   CS 0447
  //   04/17/15
  //   00 - AND
  //   01 - NOR
  //   10 - Add
  //   11 - SUB
endmodule

module ShiftControl (
  input  [3:0] Opcode,
  input  Subop,
  output LeftOrRight,
  output ShamtOrReg
);

  wire and_1_out, and_2_out, not_1_out, not_2_out, not_3_out, not_4_out, not_5_out, not_6_out, not_7_out,
       not_8_out;

  not not_1 (not_1_out, Opcode[3]);
  not not_2 (not_2_out, Opcode[2]);
  not not_3 (not_3_out, Opcode[3]);
  not not_4 (not_4_out, Opcode[1]);
  not not_5 (not_5_out, Opcode[0]);
  not not_6 (not_6_out, Opcode[3]);
  not not_7 (not_7_out, Opcode[1]);
  not not_8 (not_8_out, Opcode[0]);
  and and_1 (and_1_out, not_1_out, not_2_out, Opcode[1], Opcode[0], Subop);
  and and_2 (and_2_out, not_3_out, Opcode[2], not_4_out, not_5_out, Subop);
  and and_3 (ShamtOrReg, not_6_out, Opcode[2], not_7_out, not_8_out);
  or or_1 (LeftOrRight, and_1_out, and_2_out);

  // Notes on the sheet:
  //   Property of:
  //   Devansh Desai
  //   University of Pittsburgh
  //   CS 0447
  //   04/17/15
  //   0 - Left
  //   1 - Right
  //   0 - Use shamt
  //   1 - Use register's least signifcant nibble
endmodule

module Control__Unused (
  input  [3:0] Opcode,
  input  Subop,
  output ALUSrc,
  output MemToReg,
  output RegWrite,
  output MemRead,
  output MemWrite,
  output Branch,
  output ALUOp1,
  output ALUOp0,
  output Halt,
  output Put,
  output addi,
  output shift
);

  wire and_1_out, and_2_out, and_3_out, and_5_out, and_6_out, and_7_out, and_8_out, and_9_out, and_13_out,
       and_14_out, and_15_out, and_16_out, and_21_out, and_22_out, not_1_out, not_2_out, not_3_out,
       not_4_out, not_5_out, not_6_out, not_7_out, not_8_out, not_9_out, not_10_out, not_11_out, not_12_out,
       not_13_out, not_14_out, not_15_out, not_16_out, not_17_out, not_18_out, not_19_out, not_20_out,
       not_21_out, not_22_out, not_23_out, not_24_out, not_25_out, not_26_out, not_27_out, not_28_out,
       not_29_out, not_30_out, not_31_out, not_32_out, not_33_out, not_34_out, not_35_out, not_36_out,
       not_37_out, not_38_out;

  not not_1 (not_1_out, Opcode[3]);
  not not_2 (not_2_out, Opcode[2]);
  not not_3 (not_3_out, Opcode[0]);
  not not_4 (not_4_out, Opcode[3]);
  not not_5 (not_5_out, Opcode[1]);
  not not_6 (not_6_out, Opcode[0]);
  not not_7 (not_7_out, Opcode[3]);
  not not_8 (not_8_out, Opcode[1]);
  not not_9 (not_9_out, Subop);
  not not_10 (not_10_out, Opcode[3]);
  not not_11 (not_11_out, Opcode[2]);
  not not_12 (not_12_out, Opcode[3]);
  not not_13 (not_13_out, Opcode[0]);
  not not_14 (not_14_out, Opcode[3]);
  not not_15 (not_15_out, Subop);
  not not_16 (not_16_out, Opcode[3]);
  not not_17 (not_17_out, Opcode[3]);
  not not_18 (not_18_out, Opcode[1]);
  not not_19 (not_19_out, Subop);
  not not_20 (not_20_out, Opcode[3]);
  not not_21 (not_21_out, Opcode[1]);
  not not_22 (not_22_out, Opcode[2]);
  not not_23 (not_23_out, Opcode[3]);
  not not_24 (not_24_out, Opcode[2]);
  not not_25 (not_25_out, Opcode[3]);
  not not_26 (not_26_out, Opcode[0]);
  not not_27 (not_27_out, Opcode[3]);
  not not_28 (not_28_out, Opcode[2]);
  not not_29 (not_29_out, Opcode[0]);
  not not_30 (not_30_out, Opcode[3]);
  not not_31 (not_31_out, Opcode[3]);
  not not_32 (not_32_out, Opcode[2]);
  not not_33 (not_33_out, Opcode[0]);
  not not_34 (not_34_out, Opcode[3]);
  not not_35 (not_35_out, Opcode[2]);
  not not_36 (not_36_out, Opcode[3]);
  not not_37 (not_37_out, Opcode[1]);
  not not_38 (not_38_out, Opcode[0]);
  and and_1 (and_1_out, not_1_out, not_2_out, Opcode[1], not_3_out);
  and and_2 (and_2_out, not_4_out, Opcode[2], not_5_out, Opcode[0]);
  and and_3 (and_3_out, Opcode[3], Opcode[2], Opcode[1], not_6_out);
  and and_4 (MemToReg, not_7_out, Opcode[2], not_8_out, Opcode[0], not_9_out);
  and and_5 (and_5_out, not_10_out, not_11_out);
  and and_6 (and_6_out, not_12_out, not_13_out);
  and and_7 (and_7_out, not_14_out, not_15_out);
  and and_8 (and_8_out, not_16_out, Opcode[1]);
  and and_9 (and_9_out, Opcode[3], Opcode[2]);
  and and_10 (MemRead, not_17_out, Opcode[2], not_18_out, Opcode[0], not_19_out);
  and and_11 (MemWrite, not_20_out, Opcode[2], not_21_out, Opcode[0], Subop);
  and and_12 (Branch, Opcode[3], not_22_out);
  and and_13 (and_13_out, not_23_out, not_24_out);
  and and_14 (and_14_out, not_25_out, not_26_out);
  and and_15 (and_15_out, not_27_out, Opcode[1]);
  and and_16 (and_16_out, Opcode[3], Opcode[2]);
  and and_17 (ALUOp0, Opcode[3], not_28_out);
  and and_18 (Halt, Opcode[2], Opcode[1], not_29_out);
  and and_19 (Put, not_30_out, Opcode[2], Opcode[1], Opcode[0]);
  and and_20 (addi, not_31_out, not_32_out, Opcode[1], not_33_out);
  and and_21 (and_21_out, not_34_out, not_35_out, Opcode[1], Opcode[0]);
  and and_22 (and_22_out, not_36_out, Opcode[2], not_37_out, not_38_out);
  or or_1 (ALUSrc, and_1_out, and_2_out, and_3_out);
  or or_2 (RegWrite, and_5_out, and_6_out, and_7_out, and_8_out, and_9_out);
  or or_3 (ALUOp1, and_13_out, and_14_out, and_15_out, and_16_out);
  or or_4 (shift, and_21_out, and_22_out);

  // Notes on the sheet:
  //   Property of:
  //   Devansh Desai
  //   University of Pittsburgh
  //   CS 0447
  //   04/17/15
endmodule
